# Fritzing sketch plant_board_v01 (saved by Fritzing 0.9.3b)
circuit board: 9.72519cm x 6.6038cm

parts:
  Part2 = Arduino Nano (Rev3.0)
  D_SENSE_1 = Diode [package=diode-1n4148]
  D_SENSE_2 = Diode [package=diode-1n4148]
  R_SENSE_2 = Resistor [tolerance=±5% resistance=20k package=THT]
  R_SENSE_1 = Resistor [tolerance=±5% resistance=20k package=THT]
  SENS_1 = screw terminal, 2 pins
  I2C_BUS = screw terminal, 2 pins
  DS1 = DS18B20 1-Wire Temperature Sensor [part_number=DS18B20]
  R_SENSE_3 = Resistor [tolerance=±5% resistance=20k package=THT]
  to_2nd_temp_sensor = molex pin header, 3 pins [form=molex part_number="MOLEX 2510"]
  pump_1 = screw terminal, 2 pins
  R1 = Resistor [tolerance=±5% resistance=10k package=THT]
  Q1 = NPN-Transistor [package="TO92 [THT]"]
  12V_input = screw terminal, 2 pins

nets:
  GND: Part2.GND, R_SENSE_2.Pin_0, R_SENSE_1.Pin_0, DS1.GND, to_2nd_temp_sensor.pin3, Q1.E, 12V_input.pin2
  N1: Part2.D2, D_SENSE_1.A
  N2: Part2.D3, D_SENSE_2.A
  N3: Part2.D6, R1.Pin_0
  N4: Part2.D12/MISO, DS1.DQ, R_SENSE_3.Pin_1, to_2nd_temp_sensor.pin2
  12V: Part2.VIN, pump_1.pin1, 12V_input.pin1
  5V: Part2.5V, DS1.VDD
  SCL (to D1): Part2.A5, I2C_BUS.pin1
  SDA (to D2): Part2.A4, I2C_BUS.pin2
  N5: Part2.A1, D_SENSE_1.C, R_SENSE_1.Pin_1, SENS_1.pin2
  N6: Part2.A0, D_SENSE_2.C, R_SENSE_2.Pin_1, SENS_1.pin1
  N7: R_SENSE_3.Pin_0, to_2nd_temp_sensor.pin1
  N8: pump_1.pin2, Q1.C
  N9: R1.Pin_1, Q1.B
